// Logisim project CPU_BLOCK_CHETAN.circ as structural Verilog: 13 circuits, main circuit Decode
module main (
  input  Start_Button,
  input  AR_CLR,
  input  PC_CLR,
  input  DR_CLR,
  input  SHL,
  input  SHR,
  input  [7:0] INPR,
  input  TR_INR,
  input  TR_LD,
  input  TR_CLR,
  output E_OUT
);

  wire AC_CLR, AC_INC, AC_LD, AR_INC, AR_LD, CLK, CLK_out, DR_INC, DR_LD, E, E_CLR, E_COM, E_LD, HLT, IR_LD,
       MEMORY_READ, MEMORY_WRITE, not_1_out, PC_INC, PC_LD, r, SC_CLR;
  wire [2:0] M2M1M0, S2S1S0;
  wire [11:0] ar_1_address;
  wire [15:0] AC_OUT, alu_1_data_out, ar_1_data_out, DR_OUT, IR_OUT, multiplexer_1_out, pc_1_data_out,
       ram_1_dout, tr_1_data_out;

  Clock u_CLK (.out(CLK_out));
  not not_1 (not_1_out, HLT);
  and and_1 (CLK, Start_Button, not_1_out, CLK_out);
  EFF eff_1 (.E_COMP(E_COM), .E_LD(E_LD), .CLK(CLK), .E_DATAIN(E), .E_CLR(E_CLR), .E_OUT(E_OUT));
  ALU alu_1 (
    .DR(DR_OUT), .AC(AC_OUT), .CLK(CLK), .M2M1MO(M2M1M0), .SHL(SHL), .SHR(SHR), .INPR(INPR), .E(E),
    .DATA_OUT(alu_1_data_out));
  RAM #(.addrWidth(12), .asyncread("true"), .dataWidth(16)) ram_1 (
    .addr(ar_1_address), .we(MEMORY_WRITE), .oe(MEMORY_READ), .clk(CLK), .din(multiplexer_1_out),
    .dout(ram_1_dout));
  AR ar_1 (
    .Data_in(multiplexer_1_out), .INR(AR_INC), .LD(AR_LD), .CLR(AR_CLR), .CLK(CLK), .Data_out(ar_1_data_out),
    .Address(ar_1_address));
  DR dr_1 (.data_in(multiplexer_1_out), .INC(DR_INC), .LD(DR_LD), .CLR(DR_CLR), .CLK(CLK), .data_out(DR_OUT));
  IR ir_1 (.data_in(multiplexer_1_out), .LD(IR_LD), .CLK(CLK), .data_out(IR_OUT));
  TR tr_1 (.data_in(multiplexer_1_out), .INC(TR_INR), .LD(TR_LD), .CLR(TR_CLR), .CLK(CLK), .data_out(tr_1_data_out));
  PC pc_1 (.Data_in(multiplexer_1_out), .INR(PC_INC), .LD(PC_LD), .CLR(PC_CLR), .CLK(CLK), .Data_out(pc_1_data_out));
  AC ac_1 (.data_in(alu_1_data_out), .INC(AC_INC), .LD(AC_LD), .CLR(AC_CLR), .CLK(CLK), .data_out(AC_OUT));
  Multiplexer #(.select(3), .width(16)) multiplexer_1 (
    .in1(ar_1_data_out), .in2(pc_1_data_out), .in3(DR_OUT), .in4(AC_OUT), .in5(IR_OUT), .in6(tr_1_data_out),
    .in7(ram_1_dout), .out(multiplexer_1_out), .sel(S2S1S0));  // open: in0
  Control_unit control_unit_1 (
    .IR_IN(IR_OUT), .SC_CLR(SC_CLR), .CLK(CLK), .E(E), .AC_IN(AC_OUT), .DR_IN(DR_OUT), .r(r),
    .MEMORY_WRITE(MEMORY_WRITE), .S2S1S0(S2S1S0), .MEMORY_READ(MEMORY_READ), .SC_CLEAR(SC_CLR),
    .M2M1M0(M2M1M0), .IR_LD(IR_LD), .AC_LD(AC_LD), .PC_LD(PC_LD), .AC_INC(AC_INC), .AC_CLR(AC_CLR),
    .PC_INC(PC_INC), .AR_LD(AR_LD), .AR_INC(AR_INC), .E_LD(E_LD), .DR_LD(DR_LD), .E_CLR(E_CLR),
    .DR_INC(DR_INC), .E_CMP(E_COM), .HLT(HLT));
endmodule

module AR (
  input  [15:0] Data_in,
  input  INR,
  input  LD,
  input  CLR,
  input  CLK,
  output [15:0] Data_out,
  output [11:0] Address
);

  Register_12_bits register_12_bits_1 (
    .data_in(Data_in[11:0]), .INC(INR), .LD(LD), .CLR(CLR), .CLK(CLK), .data_out(Data_out[11:0]),
    .Address(Address));

  assign Data_in[14:12] = {3{Data_in[15]}};
  assign Data_out[15:12] = 4'b0000;
  // also tied to GND on the sheet: Data_in[15]
endmodule

module Register_12_bits (
  input  [11:0] data_in,
  input  INC,
  input  LD,
  input  CLR,
  input  CLK,
  output [11:0] data_out,
  output [11:0] Address
);

  wire [11:0] adder_1_out, multiplexer_1_out, multiplexer_2_out, multiplexer_3_out;

  Adder #(.width(12)) adder_1 (.a(12'h1), .b(Address), .out(adder_1_out));  // open: cin, cout
  Multiplexer #(.width(12)) multiplexer_1 (.in0(Address), .in1(adder_1_out), .out(multiplexer_1_out), .sel(INC));
  Multiplexer #(.width(12)) multiplexer_2 (.in0(multiplexer_1_out), .in1(data_in), .out(multiplexer_2_out), .sel(LD));
  Multiplexer #(.width(12)) multiplexer_3 (
    .in0(multiplexer_2_out), .in1({12{1'b0}}), .out(multiplexer_3_out), .sel(CLR));
  Register #(.width(12)) register_1 (.D(multiplexer_3_out), .clk(CLK), .Q(Address));  // open: en, clr

  assign data_out = Address;
endmodule

module PC (
  input  [15:0] Data_in,
  input  INR,
  input  LD,
  input  CLR,
  input  CLK,
  output [15:0] Data_out
);

  Register_12_bits register_12_bits_1 (
    .data_in(Data_in[11:0]), .INC(INR), .LD(LD), .CLR(CLR), .CLK(CLK), .data_out(Data_out[11:0]));  // open: Address

  assign Data_in[14:12] = {3{Data_in[15]}};
  assign Data_out[15:12] = 4'b0000;
  // also tied to GND on the sheet: Data_in[15]
endmodule

module DR (
  input  [15:0] data_in,
  input  INC,
  input  LD,
  input  CLR,
  input  CLK,
  output [15:0] data_out
);

  wire [15:0] adder_1_out, multiplexer_1_out, multiplexer_2_out, multiplexer_3_out;

  Adder #(.width(16)) adder_1 (.a(16'h1), .b(data_out), .out(adder_1_out));  // open: cin, cout
  Multiplexer #(.width(16)) multiplexer_1 (.in0(data_out), .in1(adder_1_out), .out(multiplexer_1_out), .sel(INC));
  Multiplexer #(.width(16)) multiplexer_2 (.in0(multiplexer_1_out), .in1(data_in), .out(multiplexer_2_out), .sel(LD));
  Multiplexer #(.width(16)) multiplexer_3 (
    .in0(multiplexer_2_out), .in1({16{1'b0}}), .out(multiplexer_3_out), .sel(CLR));
  Register #(.width(16)) register_1 (.D(multiplexer_3_out), .clk(CLK), .Q(data_out));  // open: en, clr
endmodule

module AC (
  input  [15:0] data_in,
  input  INC,
  input  LD,
  input  CLR,
  input  CLK,
  output [15:0] data_out
);

  wire [15:0] adder_1_out, multiplexer_1_out, multiplexer_2_out, multiplexer_3_out;

  Adder #(.width(16)) adder_1 (.a(16'h1), .b(data_out), .out(adder_1_out));  // open: cin, cout
  Multiplexer #(.width(16)) multiplexer_1 (.in0(data_out), .in1(adder_1_out), .out(multiplexer_1_out), .sel(INC));
  Multiplexer #(.width(16)) multiplexer_2 (.in0(multiplexer_1_out), .in1(data_in), .out(multiplexer_2_out), .sel(LD));
  Multiplexer #(.width(16)) multiplexer_3 (
    .in0(multiplexer_2_out), .in1({16{1'b0}}), .out(multiplexer_3_out), .sel(CLR));
  Register #(.width(16)) register_1 (.D(multiplexer_3_out), .clk(CLK), .Q(data_out));  // open: en, clr
endmodule

module IR (
  input  [15:0] data_in,
  input  LD,
  input  CLK,
  output [15:0] data_out
);

  wire [15:0] adder_1_out, multiplexer_1_out, multiplexer_2_out, multiplexer_3_out;

  Adder #(.width(16)) adder_1 (.a(16'h1), .b(data_out), .out(adder_1_out));  // open: cin, cout
  Multiplexer #(.width(16)) multiplexer_1 (.in0(data_out), .in1(adder_1_out), .out(multiplexer_1_out), .sel(1'b0));
  Multiplexer #(.width(16)) multiplexer_2 (.in0(multiplexer_1_out), .in1(data_in), .out(multiplexer_2_out), .sel(LD));
  Multiplexer #(.width(16)) multiplexer_3 (
    .in0(multiplexer_2_out), .in1({16{1'b0}}), .out(multiplexer_3_out), .sel(1'b0));
  Register #(.width(16)) register_1 (.D(multiplexer_3_out), .clk(CLK), .Q(data_out));  // open: en, clr
endmodule

module TR (
  input  [15:0] data_in,
  input  INC,
  input  LD,
  input  CLR,
  input  CLK,
  output [15:0] data_out
);

  wire [15:0] adder_1_out, multiplexer_1_out, multiplexer_2_out, multiplexer_3_out;

  Adder #(.width(16)) adder_1 (.a(16'h1), .b(data_out), .out(adder_1_out));  // open: cin, cout
  Multiplexer #(.width(16)) multiplexer_1 (.in0(data_out), .in1(adder_1_out), .out(multiplexer_1_out), .sel(INC));
  Multiplexer #(.width(16)) multiplexer_2 (.in0(multiplexer_1_out), .in1(data_in), .out(multiplexer_2_out), .sel(LD));
  Multiplexer #(.width(16)) multiplexer_3 (
    .in0(multiplexer_2_out), .in1({16{1'b0}}), .out(multiplexer_3_out), .sel(CLR));
  Register #(.width(16)) register_1 (.D(multiplexer_3_out), .clk(CLK), .Q(data_out));  // open: en, clr
endmodule

module ALU (
  input  [15:0] DR,
  input  [15:0] AC,
  input  CLK,
  input  [2:0] M2M1MO,
  input  SHL,
  input  SHR,
  input  [7:0] INPR,
  output E,
  output [15:0] DATA_OUT
);

  wire adder_1_cout;
  wire [15:0] adder_1_out, and_1_out, not_1_out;

  Register #(.width(1)) register_1 (.D(adder_1_cout), .en(1'b1), .clk(CLK), .Q(E));  // open: clr
  assign and_1_out = DR & AC;  // AND_Gate and_1, 16 bits wide
  Adder #(.width(16)) adder_1 (.a(DR), .b(AC), .out(adder_1_out), .cin(1'b0), .cout(adder_1_cout));
  assign not_1_out = ~AC;  // NOT_Gate not_1, 16 bits wide
  Multiplexer #(.select(3), .width(16)) multiplexer_1 (
    .in0(AC), .in1(and_1_out), .in2(adder_1_out), .in3(DR), .in4(not_1_out), .in5({SHR, AC[15:1]}),
    .in6({AC[14:0], SHL}), .in7({{8{1'b0}}, INPR}), .out(DATA_OUT), .sel(M2M1MO));
endmodule

module SUB (
  input  [15:0] DR,
  input  [15:0] AC,
  input  SHL,
  input  SHR,
  input  [7:0] INPR,
  output E,
  output [15:0] ALU_OUT
);

  wire adder_1_cout, clock_1_out;
  wire [15:0] adder_1_out, and_1_out, not_1_out;

  Register #(.width(1)) register_1 (.D(adder_1_cout), .clk(clock_1_out), .Q(E));  // open: en, clr
  Clock clock_1 (.out(clock_1_out));
  assign and_1_out = DR & AC;  // AND_Gate and_1, 16 bits wide
  Adder #(.width(16)) adder_1 (.a(DR), .b(AC), .out(adder_1_out), .cin(1'b0), .cout(adder_1_cout));
  assign not_1_out = ~AC;  // NOT_Gate not_1, 16 bits wide
  Multiplexer #(.select(3), .width(16)) multiplexer_1 (
    .in1(and_1_out), .in2(adder_1_out), .in3(DR), .in4(not_1_out), .in5({SHR, AC[15:1]}),
    .in6({AC[14:0], SHL}), .in7({{8{1'b0}}, INPR}), .out(ALU_OUT));  // open: in0, sel
endmodule

module EFF (
  input  E_COMP,
  input  E_LD,
  input  CLK,
  input  E_DATAIN,
  input  E_CLR,
  output E_OUT
);

  wire multiplexer_1_out, multiplexer_2_out, multiplexer_3_out, not_1_out;

  not not_1 (not_1_out, E_OUT);
  Multiplexer multiplexer_1 (.in0(E_OUT), .in1(not_1_out), .out(multiplexer_1_out), .sel(E_COMP));
  Multiplexer multiplexer_2 (.in0(multiplexer_1_out), .in1(E_DATAIN), .out(multiplexer_2_out), .sel(E_LD));
  Multiplexer multiplexer_3 (.in0(multiplexer_2_out), .in1(1'b0), .out(multiplexer_3_out), .sel(E_CLR));
  D_Flip_Flop d_ff_1 (.D(multiplexer_3_out), .clk(CLK), .Q(E_OUT));  // open: Qn, preset, reset
endmodule

module Decode (
  input  [15:0] IR_IN,
  input  SC_CLR,
  input  CLK,
  output I,
  output B0,
  output B1,
  output B2,
  output B3,
  output B4,
  output B5,
  output B6,
  output B7,
  output B8,
  output B9,
  output B10,
  output B11,
  output D0,
  output D1,
  output D2,
  output D3,
  output D4,
  output D5,
  output D6,
  output D7,
  output T0,
  output T1,
  output T2,
  output T3,
  output T4,
  output T5,
  output T6,
  output T7,
  output T8,
  output T9,
  output T10,
  output T11,
  output T12,
  output T13,
  output T14,
  output T15
);

  wire undriven;
  wire [3:0] adder_1_out, multiplexer_1_out, register_1_q;

  Adder #(.width(4)) adder_1 (.a(4'b0001), .b(register_1_q), .out(adder_1_out));  // open: cin, cout
  Multiplexer #(.width(4)) multiplexer_1 (.in0(adder_1_out), .in1(4'b0000), .out(multiplexer_1_out), .sel(SC_CLR));
  Register #(.width(4)) register_1 (.D(multiplexer_1_out), .en(1'b1), .clk(CLK), .Q(register_1_q), .clr(1'b0));
  Decoder #(.select(4)) decoder_1 (
    .out0(T0), .out1(T1), .out2(T2), .out3(T3), .out4(T4), .out5(T5), .out6(T6), .out7(T7), .out8(T8),
    .out9(T9), .out10(T10), .out11(T11), .out12(T12), .out13(T13), .out14(T14), .out15(T15),
    .sel(register_1_q), .en(undriven));
  Decoder #(.select(3)) decoder_2 (
    .out0(D0), .out1(D1), .out2(D2), .out3(D3), .out4(D4), .out5(D5), .out6(D6), .out7(D7),
    .sel(IR_IN[14:12]), .en(1'b1));

  assign B0 = IR_IN[0];
  assign B1 = IR_IN[1];
  assign B2 = IR_IN[2];
  assign B3 = IR_IN[3];
  assign B4 = IR_IN[4];
  assign B5 = IR_IN[5];
  assign B6 = IR_IN[6];
  assign B7 = IR_IN[7];
  assign B8 = IR_IN[8];
  assign B9 = IR_IN[9];
  assign B10 = IR_IN[10];
  assign B11 = IR_IN[11];
  assign I = IR_IN[15];
endmodule

module Control_unit (
  input  [15:0] IR_IN,
  input  SC_CLR,
  input  CLK,
  input  E,
  input  [15:0] AC_IN,
  input  [15:0] DR_IN,
  output r,
  output MEMORY_WRITE,
  output [2:0] S2S1S0,
  output MEMORY_READ,
  output SC_CLEAR,
  output [2:0] M2M1M0,
  output IR_LD,
  output AC_LD,
  output PC_LD,
  output AC_INC,
  output AC_CLR,
  output PC_INC,
  output AR_LD,
  output AR_INC,
  output E_LD,
  output DR_LD,
  output E_CLR,
  output DR_INC,
  output E_CMP,
  output HLT
);

  wire A1, A2, A3, A4, A5, A6, and_1_out, and_2_out, and_3_out, and_4_out, and_5_out, and_6_out, and_9_out,
       and_14_out, and_15_out, and_16_out, and_17_out, and_18_out, and_20_out, and_21_out, and_22_out,
       and_23_out, and_24_out, and_25_out, and_26_out, and_27_out, and_28_out, and_29_out, and_31_out,
       and_32_out, and_33_out, and_34_out, and_35_out, and_36_out, and_37_out, and_38_out, and_39_out,
       and_40_out, and_42_out, and_43_out, and_44_out, and_45_out, and_46_out, and_54_out, and_55_out, B0,
       B1, B2, B3, B4, B5, B6, B7, B8, B9, B10, B11, D0, D1, D2, D3, D4, D5, D6, D7, I, IFAC0, IFDR0,
       multiplexer_1_out, multiplexer_2_out, multiplexer_3_out, multiplexer_4_out, not_1_out, not_2_out,
       not_3_out, not_4_out, or_1_out, or_10_out, T0, T2, T3, T4, T5, T6, T7, T8, T9, T10, T11, T12, T13,
       T14, T15, X1, X2, X3, X4, X7;

  not not_1 (not_1_out, D7);
  and and_1 (and_1_out, D0, T5);
  and and_2 (and_2_out, T5, D1);
  and and_3 (and_3_out, T5, D2);
  and and_4 (and_4_out, r, B9);
  and and_5 (and_5_out, r, B7);
  and and_6 (and_6_out, r, B6);
  and and_7 (AC_INC, r, B5);
  and and_8 (AC_CLR, r, B11);
  and and_9 (and_9_out, not_1_out, I, T3);
  and and_10 (AR_INC, D5, T4);
  or or_1 (or_1_out, D0, D1, D2, D6);
  and and_11 (DR_INC, D6, T5);
  Decode decode_1 (
    .IR_IN(IR_IN), .SC_CLR(SC_CLR), .CLK(CLK), .I(I), .B0(B0), .B1(B1), .B2(B2), .B3(B3), .B4(B4), .B5(B5),
    .B6(B6), .B7(B7), .B8(B8), .B9(B9), .B10(B10), .B11(B11), .D0(D0), .D1(D1), .D2(D2), .D3(D3), .D4(D4),
    .D5(D5), .D6(D6), .D7(D7), .T0(T0), .T1(IR_LD), .T2(T2), .T3(T3), .T4(T4), .T5(T5), .T6(T6), .T7(T7),
    .T8(T8), .T9(T9), .T10(T10), .T11(T11), .T12(T12), .T13(T13), .T14(T14), .T15(T15));
  and and_12 (DR_LD, or_1_out, T4);
  and and_13 (HLT, r, B0);
  or or_2 (AR_LD, T0, T2, and_9_out);
  or or_3 (AC_LD, and_1_out, and_2_out, and_3_out, and_4_out, and_5_out, and_6_out);
  not not_2 (not_2_out, I);
  and and_14 (and_14_out, r, B4);
  and and_15 (and_15_out, r, B3);
  and and_16 (and_16_out, r, B2);
  and and_17 (and_17_out, D1, T5);
  and and_18 (and_18_out, r, B7);
  and and_19 (r, D7, not_2_out, T3);
  and and_20 (and_20_out, D3, T4);
  and and_21 (and_21_out, D5, T4);
  and and_22 (and_22_out, D6, T6);
  not not_3 (not_3_out, D7);
  and and_23 (and_23_out, not_3_out, I, T3);
  and and_24 (and_24_out, D0, T4);
  and and_25 (and_25_out, D1, T4);
  and and_26 (and_26_out, D2, T4);
  and and_27 (and_27_out, D6, T4);
  and and_28 (and_28_out, r, B1);
  and and_29 (and_29_out, r, B6);
  and and_30 (E_CMP, r, B8);
  or or_4 (MEMORY_WRITE, and_20_out, and_21_out, and_22_out);
  and and_31 (and_31_out, D0, T5);
  and and_32 (and_32_out, D1, T5);
  and and_33 (and_33_out, D2, T5);
  and and_34 (and_34_out, D5, T5);
  and and_35 (and_35_out, D3, T4);
  and and_36 (and_36_out, D4, T4);
  and and_37 (and_37_out, D6, T6);
  and and_38 (and_38_out, D4, T4);
  and and_39 (and_39_out, D5, T5);
  and and_40 (and_40_out, D6, T6);
  Multiplexer multiplexer_1 (.in0(and_40_out), .in1(1'b0), .out(multiplexer_1_out), .sel(IFDR0));
  Multiplexer multiplexer_2 (.in0(and_14_out), .in1(and_15_out), .out(multiplexer_2_out), .sel(AC_IN[15]));
  Multiplexer multiplexer_3 (.in0(and_16_out), .in1(1'b0), .out(multiplexer_3_out), .sel(IFAC0));
  Multiplexer multiplexer_4 (.in0(and_28_out), .in1(1'b0), .out(multiplexer_4_out), .sel(E));
  or or_5 (PC_LD, and_38_out, and_39_out);
  or or_6 (E_LD, and_17_out, and_18_out, and_29_out);
  or or_7 (MEMORY_READ, and_23_out, IR_LD, and_24_out, and_25_out, and_26_out, and_27_out);
  or or_8 (SC_CLEAR, 1'b0, and_31_out, and_32_out, and_33_out, and_34_out, and_35_out, and_36_out, and_37_out, r);
  or or_9 (PC_INC, IR_LD, multiplexer_1_out, multiplexer_2_out, multiplexer_3_out, multiplexer_4_out);
  and and_41 (E_CLR, r, B10);
  not not_4 (not_4_out, D7);
  and and_42 (and_42_out, D4, T4);
  and and_43 (and_43_out, D5, T5);
  and and_44 (and_44_out, D5, T4);
  and and_45 (and_45_out, D6, T6);
  and and_46 (and_46_out, D2, T5);
  or or_10 (or_10_out, D0, D1, D2, D6);
  and and_47 (A1, D2, T5);
  and and_48 (A2, D0, T5);
  and and_49 (A3, D1, T5);
  and and_50 (A4, r, B9);
  and and_51 (A5, r, B7);
  and and_52 (A6, r, B6);
  or or_11 (X1, and_42_out, and_43_out);
  and and_53 (X4, D3, T4);
  and and_54 (and_54_out, not_4_out, I, T3);
  or or_12 (X3, and_45_out, and_46_out);
  and and_55 (and_55_out, T4, or_10_out);
  or or_13 (IFDR0, DR_IN[0], DR_IN[1], DR_IN[2], DR_IN[3], DR_IN[4], DR_IN[5], DR_IN[6], DR_IN[7], DR_IN[8], DR_IN[9], DR_IN[10], DR_IN[11], DR_IN[12], DR_IN[13], DR_IN[14], DR_IN[15]);
  or or_14 (X2, T0, and_44_out);
  or or_15 (X7, IR_LD, and_54_out, and_55_out);
  or or_16 (M2M1M0[0], A1, A2, A5);
  or or_17 (M2M1M0[1], A1, A3, A6);
  or or_18 (M2M1M0[2], A4, A5, A6);
  or or_19 (S2S1S0[0], X1, X3, T2, X7);
  or or_20 (S2S1S0[1], X2, X3, X7);
  or or_21 (S2S1S0[2], X4, T2, X7);
  or or_22 (IFAC0, AC_IN[0], AC_IN[1], AC_IN[2], AC_IN[3], AC_IN[4], AC_IN[5], AC_IN[6], AC_IN[7], AC_IN[8], AC_IN[9], AC_IN[10], AC_IN[11], AC_IN[12], AC_IN[13], AC_IN[14], AC_IN[15]);

  // Other names for the same wires on the sheet: IFAC15 = AC_IN[15]; T1 = IR_LD; X5 = T2
endmodule
